// Logisim project lab8.circ as structural Verilog
module MyXOR (
  input  X,
  input  y,
  output Output
);

  wire and_1_out, and_2_out, not_1_out, not_2_out;

  not not_1 (not_1_out, X);
  not not_2 (not_2_out, y);
  and and_1 (and_1_out, not_1_out, y);
  and and_2 (and_2_out, X, not_2_out);
  or or_1 (Output, and_1_out, and_2_out);

  // Notes on the sheet:
  //   Here is a location to build an XOR circuit
  //   You can follow the tutorial (Help menu - "tutorial") or work on your own...
endmodule

module FullAdder (
  input  X,
  input  Y,
  input  CarryIn,
  output sum,
  output CarryOut,
  output S,
  output CarryOut_2
);

  wire and_1_out, and_2_out, and_3_out, and_4_out, and_5_out, and_6_out, and_7_out, not_1_out, not_2_out,
       not_3_out;

  not not_1 (not_1_out, X);
  and and_1 (and_1_out, X, Y, CarryIn);
  and and_2 (and_2_out, not_1_out, not_2_out, CarryIn);
  or or_1 (S, and_1_out, and_2_out, and_4_out, and_3_out);
  not not_2 (not_2_out, Y);
  and and_3 (and_3_out, not_1_out, Y, not_3_out);
  and and_4 (and_4_out, X, not_2_out, not_3_out);
  not not_3 (not_3_out, CarryIn);
  and and_5 (and_5_out, X, Y);
  and and_6 (and_6_out, X, CarryIn);
  or or_2 (CarryOut_2, and_5_out, and_6_out, and_7_out);
  and and_7 (and_7_out, Y, CarryIn);
endmodule

module _4_bit_Ripple_Carry_Adder (
  input  Y3,
  input  Y2,
  input  Y1,
  input  Y0,
  input  X3,
  input  X2,
  input  X1,
  input  X0,
  output Sum4,
  output Sum3,
  output Sum2,
  output Sum1,
  output Sum0
);

  wire fulladder_2_carryout_2, fulladder_3_carryout_2, fulladder_4_carryout_2;

  FullAdder fulladder_1 (
    .X(Y3), .Y(X3), .CarryIn(fulladder_2_carryout_2), .S(Sum3), .CarryOut_2(Sum4));  // open: sum, CarryOut
  FullAdder fulladder_2 (
    .X(Y2), .Y(X2), .CarryIn(fulladder_3_carryout_2), .S(Sum2), .CarryOut_2(fulladder_2_carryout_2));  // open: sum, CarryOut
  FullAdder fulladder_3 (
    .X(Y1), .Y(X1), .CarryIn(fulladder_4_carryout_2), .S(Sum1), .CarryOut_2(fulladder_3_carryout_2));  // open: sum, CarryOut
  FullAdder fulladder_4 (
    .X(Y0), .Y(X0), .CarryIn(1'b0), .S(Sum0), .CarryOut_2(fulladder_4_carryout_2));  // open: sum, CarryOut
endmodule

module _4_bit_Multiplier (
  input  Y3,
  input  Y2,
  input  Y1,
  input  Y0,
  input  X3,
  input  X2,
  input  X1,
  input  X0,
  output Z7,
  output Z6,
  output Z5,
  output Z4,
  output Z3,
  output Z2,
  output Z1,
  output Z0
);


  // Notes on the sheet:
  //   factor (4 bits)
  //   See the problem for details on this hint: perhaps build a 4x1-bit multiplier first!
  //   second factor (4 bits)
  //   product (8 bits)
  //   most significant (highest) bit
  //   least significant (lowest) bit
endmodule

module _3by2_divider (
  input  Y2,
  input  Y1,
  input  Y0,
  input  X1,
  input  X0,
  output Z2,
  output Z1,
  output Z0,
  output Error
);


  // Notes on the sheet:
  //   Dividend (3 bits: Y2 Y1 Y0)
  //   Divisor (2 bits: X1 X0)
  //   Quotient (4 bits: Z2 Z1 Z0 and Error)
endmodule
